# Fritzing sketch schema (saved by Fritzing 0.9.3b)

parts:
  DS1 = DS18B20 1-Wire Temperature Sensor [part_number=DS18B20]
  U1 = NodeMCU V3.0

nets:
  GND: DS1.GND, U1.GND
  N1: DS1.DQ, U1.D4
  VDD: DS1.VDD, U1.3V3

custom parts:
  NodeMCU V3.0: ESP8266 based NodeMCU
